// Logisim project Smart_Water_Tank_Monitoring_Control_System.circ as structural Verilog: 1 circuit, main circuit main
module main (
  input  S0,
  input  S1,
  input  S2,
  input  S3,
  input  RESET,
  output PUMP,
  output L0,
  output C1,
  output FULL,
  output out_10,
  output L1,
  output ALARM,
  output out_13,
  output Q1,
  output Q0,
  output C0
);

  wire a_out, c_out, clock_1_out, d_out, f_out, not_1_out, not_2_out, not_4_out, xor_1_out;

  and f (f_out, not_1_out, not_2_out);
  or or_1 (L0, S1, S3);
  or or_2 (L1, S2, S3);
  D_Flip_Flop d_ff_1 (.D(L1), .clk(clock_1_out), .Q(Q1), .reset(RESET));  // open: Qn, preset
  not not_1 (not_1_out, Q1);
  or c (c_out, not_1_out, Q0);
  Clock clock_1 (.out(clock_1_out));
  _7_Segment_Display u_7_segment_display_1 (
    .g(Q1), .f(f_out), .a(a_out), .b(1'b1), .e(not_2_out), .d(d_out), .c(c_out));  // open: dp
  D_Flip_Flop d_ff_2 (.D(L0), .clk(clock_1_out), .Q(Q0), .reset(RESET));  // open: Qn, preset
  or a (a_out, Q1, not_2_out);
  and and_1 (FULL, L0, L1);
  or d (d_out, Q1, not_2_out);
  not not_2 (not_2_out, Q0);
  not not_3 (PUMP, FULL);
  D_Flip_Flop d_ff_3 (.D(out_10), .clk(clock_1_out), .Q(C1), .reset(RESET));  // open: Qn, preset
  D_Flip_Flop d_ff_4 (.D(out_13), .clk(clock_1_out), .Q(C0), .reset(RESET));  // open: Qn, preset
  xor xor_1 (xor_1_out, C1, C0);
  not not_4 (not_4_out, C0);
  and and_2 (out_10, xor_1_out, FULL);
  and and_3 (out_13, FULL, not_4_out);
  and and_4 (ALARM, C1, C0);

  // Notes on the sheet:
  //   FF1
  //   FF2
  //   b
  //   b =1
  //   a = Q1 OR NOT Q0
  //   c = NOT{Q0} OR Q0
  //   d = Q1 OR NOT {Q0}
  //   e = NOT{Q0}
  //   f = NOT{Q0} AND NOT {Q1}
endmodule
